// Logisim project Bodamer_Pipeline_Logisim.circ as structural Verilog: 9 circuits, main circuit main
module main (
);

  wire CLK, comparator_1_eq, comparator_2_eq, comparator_3_eq, comparator_4_eq, comparator_5_eq,
       comparator_6_eq, comparator_7_eq, FLUSH, HALT, LdEn, LEA_GOTO, LW, not_1_out, not_2_out, or_1_out,
       or_2_out, or_3_out, or_4_out, or_5_out, or_6_out, or_7_out, or_8_out, or_9_out, or_10_out, or_11_out,
       RegWr, SKP, SKP_Success, STALL, SW, WrMem;
  wire [1:0] ALUSel, multiplexer_3_out, newPC;
  wire [2:0] rom_2_data;
  wire [3:0] EX_DR, EX_Mode, EX_Opcode, EX_SR1, ID_DR, ID_Mode, ID_Opcode, ID_SR1, ID_SR2, MEM_DR,
       MEM_Opcode, MEM_SR1, multiplexer_11_out, multiplexer_14_out, multiplexer_15_out, multiplexer_16_out,
       WB_DR, WB_Opcode, WB_SR1;
  wire [19:0] ID_IMM;
  wire [31:0] adder_1_out, adder_2_out, bit_extender_1_out, bit_extender_2_out,
       dual_ported_register_file_1_out1, EX_A, EX_ALUout, EX_B, EX_IMM, EX_PC_1,
       forwarding_unit_1_forwarded_data_1, forwarding_unit_1_forwarded_data_2, ID_A, ID_A_Forward, ID_B,
       ID_B_Forward, ID_PC_1, ID_SR2value, IF_PC, IF_PC_1, MEM_ALUout, MEM_B, MemData, multiplexer_1_out,
       multiplexer_2_out, multiplexer_4_out, multiplexer_5_out, multiplexer_6_out, multiplexer_12_out,
       multiplexer_13_out, multiplexer_17_out, multiplexer_18_out, multiplexer_19_out, multiplexer_20_out,
       rom_1_data, WB_ALUout;

  Clock clock_1 (.out(CLK));
  Adder #(.width(32)) adder_1 (.a(IF_PC), .b(32'h1), .out(adder_1_out));  // open: cin, cout
  Multiplexer #(.width(32), .disabled(0), .enable("false")) multiplexer_1 (
    .in0(IF_PC), .in1(IF_PC_1), .out(multiplexer_1_out), .sel(STALL));
  Multiplexer #(.select(2), .width(32), .disabled(0), .enable("false")) multiplexer_2 (
    .in0(adder_1_out), .in1(EX_B), .in2(EX_ALUout), .in3(IF_PC), .out(multiplexer_2_out),
    .sel(multiplexer_3_out));
  Multiplexer #(.width(2), .disabled(0), .enable("false")) multiplexer_3 (
    .in0(newPC), .in1(2'b11), .out(multiplexer_3_out), .sel(STALL));
  Subtractor #(.width(32)) subtractor_1 (.a(IF_PC), .b(32'h1), .out(IF_PC_1));  // open: bin, bout
  Register #(.width(32)) PC (.D(multiplexer_2_out), .en(CLK), .Q(IF_PC), .clk(CLK));  // open: clr
  ROM #(.addrWidth(24), .dataWidth(32)) rom_1 (.addr(multiplexer_1_out[23:0]), .data(rom_1_data));  // open: sel
  Adder #(.width(32)) adder_2 (.a(IF_PC), .b(32'h1), .out(adder_2_out));  // open: cin, cout
  Multiplexer #(.select(2), .width(32), .disabled(0), .enable("false")) multiplexer_4 (
    .in0(rom_1_data), .in1({32{1'b0}}), .in2(32'hf0000000), .in3(32'hf0000000), .out(multiplexer_4_out),
    .sel({HALT, FLUSH}));
  Multiplexer #(.width(32), .disabled(0), .enable("false")) multiplexer_5 (
    .in0(adder_2_out), .in1({32{1'b0}}), .out(multiplexer_5_out), .sel(FLUSH));
  IF_IDRR_Buffer IF_IDRR_Buffer (
    .Instruction_In(multiplexer_4_out), .Immediate(ID_IMM), .SR2(ID_SR2), .SR1_BaseR_AT(ID_SR1),
    .DR_RA(ID_DR), .Opcode(ID_Opcode), .CLK(CLK), .PC_In(multiplexer_5_out), .PC_Out(ID_PC_1), .Mode(ID_Mode));
  Multiplexer #(.width(32), .disabled(0), .enable("false")) multiplexer_6 (
    .in0(MEM_ALUout), .in1(MemData), .out(multiplexer_6_out), .sel(LdEn));
  Forwarding_Unit forwarding_unit_1 (
    .ID_Read_Reg1(ID_SR1), .ID_readReg1Data(ID_A), .ID_readReg2Data(ID_B),
    .Forwarded_Data_1(forwarding_unit_1_forwarded_data_1), .ID_Read_Reg2(ID_SR2), .ID_Write_Reg(ID_DR),
    .EX_outputReg(EX_DR), .EX_outputRegData(EX_ALUout), .MEM_outputRegData(multiplexer_6_out),
    .Forwarded_Data_2(forwarding_unit_1_forwarded_data_2), .MEM_outputReg(MEM_DR), .WB_outputReg(WB_DR),
    .WB_outputRegData(WB_ALUout));
  assign bit_extender_1_out = {{12{ID_IMM[19]}}, ID_IMM};  // Bit_Extender bit_extender_1
  ROM #(.addrWidth(4), .dataWidth(3)) rom_2 (
    .addr(ID_Opcode), .data({rom_2_data[2], LEA_GOTO, rom_2_data[0]}));  // open: sel
  Multiplexer #(.width(32), .disabled(0), .enable("false")) multiplexer_7 (
    .in0(ID_SR2value), .in1(bit_extender_1_out), .out(ID_B), .sel(rom_2_data[0]));
  or or_1 (or_1_out, FLUSH, SKP_Success);
  not not_1 (not_1_out, or_1_out);
  Dual_Ported_Register_File dual_ported_register_file_1 (
    .CLK(CLK), .WrREGNO(WB_DR), .RdREGNO1(ID_SR1), .RdREGNO2(ID_SR2), .INPUT(WB_ALUout),
    .OUT1(dual_ported_register_file_1_out1), .OUT2(ID_SR2value), .WrEN(RegWr));
  and and_1 (HALT, rom_2_data[2], not_1_out);
  Multiplexer #(.width(32), .disabled(0), .enable("false")) multiplexer_8 (
    .in0(dual_ported_register_file_1_out1), .in1(ID_PC_1), .out(ID_A), .sel(LEA_GOTO));
  Multiplexer #(.width(32), .disabled(0), .enable("false")) multiplexer_9 (
    .in0(forwarding_unit_1_forwarded_data_1), .in1(ID_A), .out(ID_A_Forward), .sel(comparator_1_eq));
  Comparator #(.width(4), .mode("unsigned")) comparator_1 (
    .a(ID_SR1), .b(4'b0000), .eq(comparator_1_eq));  // open: gt, lt
  Multiplexer #(.width(32), .disabled(0), .enable("false")) multiplexer_10 (
    .in0(forwarding_unit_1_forwarded_data_2), .in1(ID_B), .out(ID_B_Forward), .sel(comparator_2_eq));
  Comparator #(.width(4), .mode("unsigned")) comparator_2 (
    .a(ID_SR2), .b(4'b0000), .eq(comparator_2_eq));  // open: gt, lt
  or or_2 (or_2_out, STALL, SKP_Success, FLUSH);
  assign bit_extender_2_out = {{12{ID_IMM[19]}}, ID_IMM};  // Bit_Extender bit_extender_2
  Multiplexer #(.width(4), .disabled(0), .enable("false")) multiplexer_11 (
    .in0(ID_SR1), .in1(4'b0000), .out(multiplexer_11_out), .sel(or_2_out));
  Multiplexer #(.width(32), .disabled(0), .enable("false")) multiplexer_12 (
    .in0(ID_A_Forward), .in1({32{1'b0}}), .out(multiplexer_12_out), .sel(or_3_out));
  or or_3 (or_3_out, STALL, SKP_Success, FLUSH);
  Multiplexer #(.width(32), .disabled(0), .enable("false")) multiplexer_13 (
    .in0(ID_B_Forward), .in1({32{1'b0}}), .out(multiplexer_13_out), .sel(or_4_out));
  or or_4 (or_4_out, STALL, SKP_Success, FLUSH);
  Multiplexer #(.width(4), .disabled(0), .enable("false")) multiplexer_14 (
    .in0(ID_Opcode), .in1(4'b0000), .out(multiplexer_14_out), .sel(or_5_out));
  or or_5 (or_5_out, STALL, SKP_Success, FLUSH);
  Multiplexer #(.width(4), .disabled(0), .enable("false")) multiplexer_15 (
    .in0(ID_Mode), .in1(4'b0000), .out(multiplexer_15_out), .sel(or_6_out));
  or or_6 (or_6_out, STALL, SKP_Success, FLUSH);
  Multiplexer #(.width(4), .disabled(0), .enable("false")) multiplexer_16 (
    .in0(ID_DR), .in1(4'b0000), .out(multiplexer_16_out), .sel(or_7_out));
  or or_7 (or_7_out, STALL, SKP_Success, FLUSH);
  Multiplexer #(.width(32), .disabled(0), .enable("false")) multiplexer_17 (
    .in0(bit_extender_2_out), .in1({32{1'b0}}), .out(multiplexer_17_out), .sel(or_8_out));
  or or_8 (or_8_out, STALL, SKP_Success, FLUSH);
  Multiplexer #(.width(32), .disabled(0), .enable("false")) multiplexer_18 (
    .in0(ID_PC_1), .in1({32{1'b0}}), .out(multiplexer_18_out), .sel(or_9_out));
  or or_9 (or_9_out, STALL, SKP_Success, FLUSH);
  IDRR_EX_Buffer IDRR_EX_Buffer (
    .A_in(multiplexer_12_out), .B_in(multiplexer_13_out), .Opcode_in(multiplexer_14_out), .A_out(EX_A),
    .B_out(EX_B), .Opcode_out(EX_Opcode), .CLK(CLK), .DR_in(multiplexer_16_out), .DR_out(EX_DR),
    .SW_value_in(multiplexer_17_out), .SW_value_out(EX_IMM), .SR_in(multiplexer_11_out), .SR_out(EX_SR1),
    .PC_1_in(multiplexer_18_out), .PC_1_out(EX_PC_1), .Mode_in(multiplexer_15_out), .Mode_out(EX_Mode));
  Multiplexer #(.width(32), .disabled(0), .enable("false")) multiplexer_19 (
    .in0(EX_B), .in1(EX_IMM), .out(multiplexer_19_out), .sel(SW));
  ALU alu_1 (.A(EX_A), .B(multiplexer_19_out), .Select(ALUSel), .Output(EX_ALUout));
  Comparison_Logic comparison_logic_1 (.A_B(EX_ALUout), .SKP_Success(SKP_Success), .mode(EX_Mode), .SKP(SKP));
  Comparator #(.width(4)) comparator_3 (.a(ID_SR1), .b(EX_DR), .eq(comparator_3_eq));  // open: gt, lt
  Comparator #(.width(4)) comparator_4 (.a(ID_SR2), .b(EX_DR), .eq(comparator_4_eq));  // open: gt, lt
  Comparator #(.width(32)) comparator_5 (.a(EX_B), .b(EX_PC_1), .eq(comparator_5_eq));  // open: gt, lt
  Comparator #(.width(4)) comparator_6 (.a(EX_Opcode), .b(4'b1100), .eq(comparator_6_eq));  // open: gt, lt
  Comparator #(.width(4)) comparator_7 (.a(EX_Opcode), .b(4'b0100), .eq(comparator_7_eq));  // open: gt, lt
  ROM #(.addrWidth(4), .dataWidth(7)) rom_3 (.addr(EX_Opcode), .data({SW, SKP, LW, newPC, ALUSel}));  // open: sel
  or or_10 (or_10_out, comparator_3_eq, comparator_4_eq);
  not not_2 (not_2_out, comparator_5_eq);
  or or_11 (or_11_out, comparator_6_eq, comparator_7_eq);
  and and_2 (STALL, or_10_out, LW);
  and and_3 (FLUSH, not_2_out, or_11_out);
  EX_MEM_Buffer EX_MEM_Buffer (
    .ALU_in(EX_ALUout), .Opcode_in(EX_Opcode), .ALU_out(MEM_ALUout), .Opcode_out(MEM_Opcode), .CLK(CLK),
    .DR_in(EX_DR), .DR_out(MEM_DR), .SW_value_in(EX_B), .SW_value_out(MEM_B), .SR1_in(EX_SR1),
    .SR1_out(MEM_SR1));
  RAM #(.addrWidth(24), .dataWidth(32), .bus("separate")) ram_1 (
    .addr(MEM_ALUout[23:0]), .din(MEM_B), .data(MemData), .str(WrMem), .clk(CLK), .ld(LdEn));  // open: sel, clr
  ROM #(.addrWidth(4), .dataWidth(2)) rom_4 (.addr(MEM_Opcode), .data({LdEn, WrMem}));  // open: sel
  MEM_WB_Buffer MEM_WB_Buffer (
    .WB_value_in(multiplexer_20_out), .DR_in(MEM_DR), .CLK(CLK), .WB_value_out(WB_ALUout), .DR_out(WB_DR),
    .Opcode_in(MEM_Opcode), .Opcode_out(WB_Opcode), .SR1_in(MEM_SR1), .SR1_out(WB_SR1));
  Multiplexer #(.width(32), .disabled(0), .enable("false")) multiplexer_20 (
    .in0(MEM_ALUout), .in1(MemData), .out(multiplexer_20_out), .sel(LdEn));
  ROM #(.addrWidth(4), .dataWidth(1)) rom_5 (.addr(WB_Opcode), .data(RegWr));  // open: sel

  // Notes on the sheet:
  //   Fetch
  //   Instruction ROM
  //   contents of rom_1 (hex, n*v repeats v):
  //   5d00002e 8dd00000 53000008 83300000 54000007 84400000 51000007 c1f00000 53000004 92300000 f0000000 2
  //   a 0 1ddfffff 9ed00000 1ed00000 31400000 4000000f 31300000 4000000f 144fffff 510ffff7 1ddffffe
  //   9fefffff 93effffe c1f00000 4200000 83effffe 5100000a c1f00000 8fefffff 1dd00002 40000003 12000001
  //   31200000 2000000 8ee00000 1dd00001 cf000000 2000000 16000001 2200003 16600001 31600004 400ffffc
  //   cf000000 a00000
  //   Decode
  //   contents of rom_2 (hex, n*v repeats v):
  //   0 1 0 0 3 3 0 0 1 0 0 0 2 0 0 4
  //   Execute
  //   contents of rom_3 (hex, n*v repeats v):
  //   0 0 2 21 8 0 0 0 10 40 0 0 7
  //   Memory
  //   Data RAM
  //   contents of rom_4 (hex, n*v repeats v):
  //   8*0 2 1
  //   Writeback
  //   contents of rom_5 (hex, n*v repeats v):
  //   1 1 1 0 0 1 0 0 1 0 0 0 1
endmodule

module Dual_Ported_Register_File (
  input  CLK,
  input  WrEN,
  input  [3:0] WrREGNO,
  input  [3:0] RdREGNO1,
  input  [3:0] RdREGNO2,
  input  [31:0] INPUT,
  output [31:0] OUT1,
  output [31:0] OUT2
);

  wire En_a0, En_a1, En_a2, En_at, En_fp, En_k0, En_ra, En_s0, En_s1, En_s2, En_sp, En_t0, En_t1, En_t2,
       En_v0;
  wire [31:0] a0, a1, a2, at, fp, k0, ra, s0, s1, s2, sp, t0, t1, t2, v0, zero;

  Decoder #(.select(4), .disabled(0)) decoder_1 (
    .out1(En_at), .out2(En_v0), .out3(En_a0), .out4(En_a1), .out5(En_a2), .out6(En_t0), .out7(En_t1),
    .out8(En_t2), .out9(En_s0), .out10(En_s1), .out11(En_s2), .out12(En_k0), .out13(En_sp), .out14(En_fp),
    .out15(En_ra), .sel(WrREGNO), .en(WrEN));  // open: out0
  Register #(.width(32)) u_zero (.D(INPUT), .en(1'b0), .Q(zero), .clk(CLK));  // open: clr
  Register #(.width(32)) u_at (.D(INPUT), .en(En_at), .Q(at), .clk(CLK));  // open: clr
  Register #(.width(32)) u_v0 (.D(INPUT), .en(En_v0), .Q(v0), .clk(CLK));  // open: clr
  Register #(.width(32)) u_a0 (.D(INPUT), .en(En_a0), .Q(a0), .clk(CLK));  // open: clr
  Register #(.width(32)) u_a1 (.D(INPUT), .en(En_a1), .Q(a1), .clk(CLK));  // open: clr
  Register #(.width(32)) u_a2 (.D(INPUT), .en(En_a2), .Q(a2), .clk(CLK));  // open: clr
  Register #(.width(32)) u_t0 (.D(INPUT), .en(En_t0), .Q(t0), .clk(CLK));  // open: clr
  Register #(.width(32)) u_t1 (.D(INPUT), .en(En_t1), .Q(t1), .clk(CLK));  // open: clr
  Multiplexer #(.select(4), .width(32), .disabled(0), .enable("false")) multiplexer_1 (
    .in0(zero), .in1(at), .in2(v0), .in3(a0), .in4(a1), .in5(a2), .in6(t0), .in7(t1), .in8(t2), .in9(s0),
    .in10(s1), .in11(s2), .in12(k0), .in13(sp), .in14(fp), .in15(ra), .out(OUT2), .sel(RdREGNO2));
  Register #(.width(32)) u_t2 (.D(INPUT), .en(En_t2), .Q(t2), .clk(CLK));  // open: clr
  Register #(.width(32)) u_s0 (.D(INPUT), .en(En_s0), .Q(s0), .clk(CLK));  // open: clr
  Register #(.width(32)) u_s1 (.D(INPUT), .en(En_s1), .Q(s1), .clk(CLK));  // open: clr
  Register #(.width(32)) u_s2 (.D(INPUT), .en(En_s2), .Q(s2), .clk(CLK));  // open: clr
  Register #(.width(32)) u_k0 (.D(INPUT), .en(En_k0), .Q(k0), .clk(CLK));  // open: clr
  Register #(.width(32)) u_sp (.D(INPUT), .en(En_sp), .Q(sp), .clk(CLK));  // open: clr
  Register #(.width(32)) u_fp (.D(INPUT), .en(En_fp), .Q(fp), .clk(CLK));  // open: clr
  Register #(.width(32)) u_ra (.D(INPUT), .en(En_ra), .Q(ra), .clk(CLK));  // open: clr
  Multiplexer #(.select(4), .width(32), .disabled(0), .enable("false")) multiplexer_2 (
    .in0(zero), .in1(at), .in2(v0), .in3(a0), .in4(a1), .in5(a2), .in6(t0), .in7(t1), .in8(t2), .in9(s0),
    .in10(s1), .in11(s2), .in12(k0), .in13(sp), .in14(fp), .in15(ra), .out(OUT1), .sel(RdREGNO1));
endmodule

module IF_IDRR_Buffer (
  input  CLK,
  input  [31:0] Instruction_In,
  input  [31:0] PC_In,
  output [3:0] Mode,
  output [3:0] Opcode,
  output [3:0] DR_RA,
  output [31:0] PC_Out,
  output [3:0] SR1_BaseR_AT,
  output [3:0] SR2,
  output [19:0] Immediate
);

  wire ImmSel, modeSel;
  wire [1:0] DRSel, SR1Sel, SR2Sel;
  wire [3:0] _0_3, _20_23, _24_27;
  wire [19:4] _0_19;

  ROM #(.addrWidth(4)) rom_1 (.addr(Opcode), .data({SR2Sel, SR1Sel, DRSel, ImmSel, modeSel}));  // open: sel
  Register #(.width(32)) PC (.D(PC_In), .en(CLK), .Q(PC_Out), .clk(CLK));  // open: clr
  Register #(.width(32)) Instruction (
    .D(Instruction_In), .en(CLK), .Q({Opcode, _24_27, _20_23, _0_19, _0_3}), .clk(CLK));  // open: clr
  Multiplexer #(.select(2), .width(4), .disabled(0), .enable("false")) multiplexer_1 (
    .in0(4'b0000), .in1(_0_3), .in2(_24_27), .out(SR2), .sel(SR2Sel));  // open: in3
  Multiplexer #(.select(2), .width(4), .disabled(0), .enable("false")) multiplexer_2 (
    .in0(4'b0000), .in1(_20_23), .in2(_24_27), .out(SR1_BaseR_AT), .sel(SR1Sel));  // open: in3
  Multiplexer #(.select(2), .width(4), .disabled(0), .enable("false")) multiplexer_3 (
    .in0(4'b0000), .in1(_20_23), .in2(_24_27), .out(DR_RA), .sel(DRSel));  // open: in3
  Multiplexer #(.width(20), .disabled(0), .enable("false")) multiplexer_4 (
    .in0({20{1'b0}}), .in1({_0_19, _0_3}), .out(Immediate), .sel(ImmSel));
  Multiplexer #(.width(4), .disabled(0), .enable("false")) multiplexer_5 (
    .in0(4'b0000), .in1(_24_27), .out(Mode), .sel(modeSel));

  // Other names for the same wires on the sheet: _0_19[3:0] = _0_3

  // Notes on the sheet:
  //   contents of rom_1 (hex, n*v repeats v):
  //   58 1a 58 51 2 a 0 0 1a 92 0 0 84
endmodule

module IDRR_EX_Buffer (
  input  CLK,
  input  [31:0] A_in,
  input  [31:0] B_in,
  input  [31:0] PC_1_in,
  input  [3:0] Opcode_in,
  input  [3:0] SR_in,
  input  [3:0] DR_in,
  input  [31:0] SW_value_in,
  input  [3:0] Mode_in,
  output [31:0] A_out,
  output [31:0] B_out,
  output [31:0] PC_1_out,
  output [3:0] Opcode_out,
  output [3:0] SR_out,
  output [3:0] DR_out,
  output [31:0] SW_value_out,
  output [3:0] Mode_out
);

  Register #(.width(32)) A (.D(A_in), .en(CLK), .Q(A_out), .clk(CLK));  // open: clr
  Register #(.width(32)) B (.D(B_in), .en(CLK), .Q(B_out), .clk(CLK));  // open: clr
  Register #(.width(4)) Opcode (.D(Opcode_in), .en(CLK), .Q(Opcode_out), .clk(CLK));  // open: clr
  Register #(.width(4)) DR_num (.D(DR_in), .en(CLK), .Q(DR_out), .clk(CLK));  // open: clr
  Register #(.width(32)) SW_Value (.D(SW_value_in), .en(CLK), .Q(SW_value_out), .clk(CLK));  // open: clr
  Register #(.width(4)) SR1_num (.D(SR_in), .en(CLK), .Q(SR_out), .clk(CLK));  // open: clr
  Register #(.width(32)) PC_1 (.D(PC_1_in), .en(CLK), .Q(PC_1_out), .clk(CLK));  // open: clr
  Register #(.width(4)) Mode (.D(Mode_in), .en(CLK), .Q(Mode_out), .clk(CLK));  // open: clr
endmodule

module EX_MEM_Buffer (
  input  CLK,
  input  [31:0] ALU_in,
  input  [3:0] Opcode_in,
  input  [3:0] DR_in,
  input  [3:0] SR1_in,
  input  [31:0] SW_value_in,
  output [31:0] ALU_out,
  output [3:0] Opcode_out,
  output [3:0] DR_out,
  output [3:0] SR1_out,
  output [31:0] SW_value_out
);

  Register #(.width(32)) u_ALU_Out (.D(ALU_in), .en(CLK), .Q(ALU_out), .clk(CLK));  // open: clr
  Register #(.width(4)) register_1 (.D(Opcode_in), .en(CLK), .Q(Opcode_out), .clk(CLK));  // open: clr
  Register #(.width(4)) DR_num (.D(DR_in), .en(CLK), .Q(DR_out), .clk(CLK));  // open: clr
  Register #(.width(32)) SW_Value (.D(SW_value_in), .en(CLK), .Q(SW_value_out), .clk(CLK));  // open: clr
  Register #(.width(4)) SR1_num (.D(SR1_in), .en(CLK), .Q(SR1_out), .clk(CLK));  // open: clr
endmodule

module MEM_WB_Buffer (
  input  CLK,
  input  [31:0] WB_value_in,
  input  [3:0] DR_in,
  input  [3:0] Opcode_in,
  input  [3:0] SR1_in,
  output [31:0] WB_value_out,
  output [3:0] DR_out,
  output [3:0] Opcode_out,
  output [3:0] SR1_out
);

  Register #(.width(32)) WB_value (.D(WB_value_in), .en(CLK), .Q(WB_value_out), .clk(CLK));  // open: clr
  Register #(.width(4)) DR_num (.D(DR_in), .en(CLK), .Q(DR_out), .clk(CLK));  // open: clr
  Register #(.width(4)) Opcode (.D(Opcode_in), .en(CLK), .Q(Opcode_out), .clk(CLK));  // open: clr
  Register #(.width(4)) SR1_num (.D(SR1_in), .en(CLK), .Q(SR1_out), .clk(CLK));  // open: clr
endmodule

module Forwarding_Unit (
  input  [3:0] ID_Read_Reg1,
  input  [31:0] ID_readReg1Data,
  input  [31:0] ID_readReg2Data,
  input  [3:0] ID_Read_Reg2,
  input  [3:0] ID_Write_Reg,
  input  [3:0] EX_outputReg,
  input  [31:0] EX_outputRegData,
  input  [31:0] MEM_outputRegData,
  input  [3:0] MEM_outputReg,
  input  [3:0] WB_outputReg,
  input  [31:0] WB_outputRegData,
  output [31:0] Forwarded_Data_1,
  output [31:0] Forwarded_Data_2
);

  wire comparator_1_eq, comparator_2_eq, comparator_3_eq, comparator_4_eq, comparator_5_eq, comparator_6_eq;
  wire [1:0] pull_resistor_1_node, pull_resistor_2_node;

  Comparator #(.width(4)) comparator_1 (.a(WB_outputReg), .b(ID_Read_Reg1), .eq(comparator_1_eq));  // open: gt, lt
  Comparator #(.width(4)) comparator_2 (.a(MEM_outputReg), .b(ID_Read_Reg1), .eq(comparator_2_eq));  // open: gt, lt
  Comparator #(.width(4)) comparator_3 (.a(EX_outputReg), .b(ID_Read_Reg1), .eq(comparator_3_eq));  // open: gt, lt
  Pull_Resistor pull_resistor_1 (.node(pull_resistor_1_node));
  Priority_Encoder #(.select(2)) priority_encoder_1 (
    .in1(comparator_1_eq), .in2(comparator_2_eq), .in3(comparator_3_eq), .out(pull_resistor_1_node));  // open: in0, gs, en_out, en_in
  Multiplexer #(.select(2), .width(32), .disabled(0), .enable("false")) multiplexer_1 (
    .in0(ID_readReg1Data), .in1(WB_outputRegData), .in2(MEM_outputRegData), .in3(EX_outputRegData),
    .out(Forwarded_Data_1), .sel(pull_resistor_1_node));
  Comparator #(.width(4)) comparator_4 (.a(WB_outputReg), .b(ID_Read_Reg2), .eq(comparator_4_eq));  // open: gt, lt
  Comparator #(.width(4)) comparator_5 (.a(MEM_outputReg), .b(ID_Read_Reg2), .eq(comparator_5_eq));  // open: gt, lt
  Comparator #(.width(4)) comparator_6 (.a(EX_outputReg), .b(ID_Read_Reg2), .eq(comparator_6_eq));  // open: gt, lt
  Pull_Resistor pull_resistor_2 (.node(pull_resistor_2_node));
  Priority_Encoder #(.select(2)) priority_encoder_2 (
    .in1(comparator_4_eq), .in2(comparator_5_eq), .in3(comparator_6_eq), .out(pull_resistor_2_node));  // open: in0, gs, en_out, en_in
  Multiplexer #(.select(2), .width(32), .disabled(0), .enable("false")) multiplexer_2 (
    .in0(ID_readReg2Data), .in1(WB_outputRegData), .in2(MEM_outputRegData), .in3(EX_outputRegData),
    .out(Forwarded_Data_2), .sel(pull_resistor_2_node));

  // Other names for the same wires on the sheet: EX_DR[3:0] = EX_outputReg; ID_DR[3:0] = ID_Write_Reg;
  //   ID_SR1[3:0] = ID_Read_Reg1; ID_SR2[3:0] = ID_Read_Reg2; MEM_DR[3:0] = MEM_outputReg; WB_DR[3:0] = WB_outputReg
endmodule

module ALU (
  input  [31:0] A,
  input  [31:0] B,
  input  [1:0] Select,
  output [31:0] Output
);

  wire [31:0] adder_1_out, adder_2_out, nand_1_out, subtractor_1_out;

  Adder #(.width(32)) adder_1 (.a(A), .b(B), .out(adder_1_out));  // open: cin, cout
  Subtractor #(.width(32)) subtractor_1 (.a(A), .b(B), .out(subtractor_1_out));  // open: bin, bout
  assign nand_1_out = ~(A & B);  // NAND_Gate nand_1, 32 bits wide
  Adder #(.width(32)) adder_2 (.a(A), .b({32{1'b0}}), .out(adder_2_out));  // open: cin, cout
  Multiplexer #(.select(2), .width(32), .disabled(0), .enable("false")) multiplexer_1 (
    .in0(adder_1_out), .in1(subtractor_1_out), .in2(nand_1_out), .in3(adder_2_out), .out(Output), .sel(Select));
endmodule

module Comparison_Logic (
  input  [31:0] A_B,
  input  SKP,
  input  [3:0] mode,
  output SKP_Success
);

  wire comparator_1_eq, comparator_1_gt, not_1_out;

  Comparator #(.width(32)) comparator_1 (
    .a(A_B), .b({32{1'b0}}), .gt(comparator_1_gt), .eq(comparator_1_eq));  // open: lt
  Multiplexer #(.disabled(0)) multiplexer_1 (
    .in0(comparator_1_gt), .in1(comparator_1_eq), .out(SKP_Success), .sel(not_1_out), .en(SKP));
  not not_1 (not_1_out, mode[0]);
  Pull_Resistor pull_resistor_1 (.node(SKP));
endmodule
